# Fritzing sketch ControlSchematic (saved by Fritzing 0.8.7b)
circuit board: 13.8023cm x 5.26209cm
breadboards: 1

parts:
  Raspberry_Pi = Raspberry Pi B rev2
  DRV1 = A4983
  M1 = Stepper Motor - Bipolar
  12V_PSU = Power Jack [package=power_jack_pth_lock]
  C1 = Electrolytic Capacitor [capacitance=0.1mF package="100 mil [THT, electrolytic]"]
  DRV2 = A4983
  M2 = Stepper Motor - Bipolar
  DRV3 = A4983
  M3 = Stepper Motor - Bipolar
  DRV4 = A4983
  M4 = Stepper Motor - Bipolar
  THERM = female pin header, 2 pins [form="♀ (female)"]
  C2 = Electrolytic Capacitor [capacitance=10µF package="100 mil [THT, electrolytic]"]
  R1 = Resistor [tolerance=±5% resistance=4.7k package=THT]
  HOTEND = female pin header, 4 pins [form="♀ (female)"]
  Q1 = Basic FET N-Channel [package="TO220 [THT]"]
  R2 = Resistor [tolerance=±5% resistance=10k package=THT]
  J1 = double row male pin header, 6 pins [form="♂ (male)"]
  J2 = double row male pin header, 6 pins [form="♂ (male)"]
  J3 = double row male pin header, 6 pins [form="♂ (male)"]
  J4 = double row male pin header, 6 pins [form="♂ (male)"]
  MCP3002 = IC, DIP package, 8 pins [chip_label=IC]

nets:
  3V3: Raspberry_Pi.3V3, DRV1.VDD, DRV2.VDD, DRV3.VDD, DRV4.VDD, R1.Pin_1, J1.pin4, J1.pin5, J1.pin6, J2.pin4, J2.pin5, J2.pin6, J3.pin4, J3.pin5, J3.pin6, J4.pin4, J4.pin5, J4.pin6, MCP3002.pin8
  GND: Raspberry_Pi.GND, DRV1.GNDMOT, DRV1.GND, 12V_PSU.GND, C1.-, DRV2.GNDMOT, DRV2.GND, DRV3.GNDMOT, DRV3.GND, DRV4.GNDMOT, DRV4.GND, THERM.pin2, C2.-, Q1.source, R2.Pin_0, MCP3002.pin4
  DIR2: Raspberry_Pi.GPIO_23, DRV2.DIR
  STEP1: Raspberry_Pi.GPIO_14, DRV1.STEP
  DIR1: Raspberry_Pi.GPIO_15, DRV1.DIR
  STEP2: Raspberry_Pi.GPIO_18, DRV2.STEP
  ENABLE: Raspberry_Pi.GPIO_27, DRV1.EN, DRV2.EN, DRV3.EN, DRV4.EN
  STEP4: Raspberry_Pi.GPIO_22, DRV4.STEP
  CLK: Raspberry_Pi.GPIO_4, MCP3002.pin7
  STEP3: Raspberry_Pi.GPIO_24, DRV3.STEP
  MOSI: Raspberry_Pi.GPIO_10, MCP3002.pin5
  MISO: Raspberry_Pi.GPIO_9, MCP3002.pin6
  DIR3: Raspberry_Pi.GPIO_25, DRV3.DIR
  HOTEND: Raspberry_Pi.GPIO_11, Q1.gate, R2.Pin_1
  CS0: Raspberry_Pi.GPIO_8, MCP3002.pin1
  DIR4: Raspberry_Pi.GPIO_7, DRV4.DIR
  N1: DRV1.MS1, J1.pin1
  N2: DRV1.MS2, J1.pin2
  N3: DRV1.MS3, J1.pin3
  N4: DRV1.RST, DRV1.SLP
  12V: DRV1.VMOT, 12V_PSU.PWR, C1.+, DRV2.VMOT, DRV3.VMOT, DRV4.VMOT, HOTEND.pin1, HOTEND.pin2
  N5: DRV1.2B, M1.A
  N6: DRV1.2A, M1.C
  N7: DRV1.1A, M1.B
  N8: DRV1.1B, M1.D
  N9: DRV2.MS1, J2.pin1
  N10: DRV2.MS2, J2.pin2
  N11: DRV2.MS3, J2.pin3
  N12: DRV2.RST, DRV2.SLP
  N13: DRV2.2B, M2.A
  N14: DRV2.2A, M2.C
  N15: DRV2.1A, M2.B
  N16: DRV2.1B, M2.D
  N17: DRV3.MS1, J3.pin1
  N18: DRV3.MS2, J3.pin2
  N19: DRV3.MS3, J3.pin3
  N20: DRV3.RST, DRV3.SLP
  N21: DRV3.2B, M3.A
  N22: DRV3.2A, M3.C
  N23: DRV3.1A, M3.B
  N24: DRV3.1B, M3.D
  N25: DRV4.MS1, J4.pin1
  N26: DRV4.MS2, J4.pin2
  N27: DRV4.MS3, J4.pin3
  N28: DRV4.RST, DRV4.SLP
  N29: DRV4.2B, M4.A
  N30: DRV4.2A, M4.C
  N31: DRV4.1A, M4.B
  N32: DRV4.1B, M4.D
  N33: THERM.pin1, C2.+, R1.Pin_0, MCP3002.pin2
  N34: HOTEND.pin3, HOTEND.pin4, Q1.drain

notes:
  PiRap, Raspberry Pi RepRap Control Board, 0.1

custom parts:
  A4983: Poloko A4983 Stepper Motor Control Breakout
