# Fritzing sketch ControlSchematic (saved by Fritzing 0.8.7b)
circuit board: 11.2011cm x 6.92721cm
breadboards: 1

parts:
  M1 = Stepper Motor - Bipolar
  12V_PSU = Power Jack [package=power_jack_pth_lock]
  M2 = Stepper Motor - Bipolar
  DRV3 = A4983
  M3 = Stepper Motor - Bipolar
  DRV4 = A4983
  M4 = Stepper Motor - Bipolar
  THERM1 = female pin header, 2 pins [form="♀ (female)"]
  C2 = Electrolytic Capacitor [capacitance=10µF package="100 mil [THT, electrolytic]"]
  HOTEND = female pin header, 4 pins [form="♀ (female)"]
  Q1 = Basic FET N-Channel [package="TO220 [THT]"]
  R2 = Resistor [tolerance=±5% resistance=10k package=THT]
  J1 = double row male pin header, 6 pins [form="♂ (male)"]
  J2 = double row male pin header, 6 pins [form="♂ (male)"]
  J3 = double row male pin header, 6 pins [form="♂ (male)"]
  J4 = double row male pin header, 6 pins [form="♂ (male)"]
  MCP3002 = IC, DIP package, 8 pins [chip_label=IC]
  THERM2 = female pin header, 2 pins [form="♀ (female)"]
  C7 = Electrolytic Capacitor [capacitance=10µF package="100 mil [THT, electrolytic]"]
  R3 = Resistor [tolerance=±5% resistance=4.7k package=THT]
  HOTBED = female pin header, 4 pins [form="♀ (female)"]
  Q2 = Basic FET N-Channel [package="TO220 [THT]"]
  R4 = Resistor [tolerance=±5% resistance=10k package=THT]
  R1 = Resistor [tolerance=±5% resistance=4.7k package=THT]
  C5 = Electrolytic Capacitor [capacitance=0.1mF package="100 mil [THT, electrolytic]"]
  C6 = Electrolytic Capacitor [capacitance=0.1mF package="100 mil [THT, electrolytic]"]
  C4 = Electrolytic Capacitor [capacitance=0.1mF package="100 mil [THT, electrolytic]"]
  C3 = Electrolytic Capacitor [capacitance=0.1mF package="100 mil [THT, electrolytic]"]
  DRV1 = A4983
  DRV2 = A4983
  Raspberry_Pi = Raspberry Pi B rev1

nets:
  N1: M1.A, DRV1.2B
  N2: M1.C, DRV1.2A
  N3: M1.B, DRV1.1A
  N4: M1.D, DRV1.1B
  GND: 12V_PSU.GND, DRV3.GNDMOT, DRV3.GND, DRV4.GNDMOT, DRV4.GND, THERM1.pin2, C2.-, Q1.source, R2.Pin_0, MCP3002.pin4, THERM2.pin2, C7.-, Q2.source, R4.Pin_0, C5.-, C6.-, C4.-, C3.-, DRV1.GNDMOT, DRV1.GND, DRV2.GNDMOT, DRV2.GND, Raspberry_Pi.GND
  12V: 12V_PSU.PWR, DRV3.VMOT, DRV4.VMOT, HOTEND.pin1, HOTEND.pin2, HOTBED.pin1, HOTBED.pin2, C5.+, C6.+, C4.+, C3.+, DRV1.VMOT, DRV2.VMOT
  N5: M2.A, DRV2.2B
  N6: M2.C, DRV2.2A
  N7: M2.B, DRV2.1A
  N8: M2.D, DRV2.1B
  N9: DRV3.MS1, J3.pin1
  N10: DRV3.MS2, J3.pin2
  N11: DRV3.MS3, J3.pin3
  N12: DRV3.RST, DRV3.SLP
  STEP3: DRV3.STEP, Raspberry_Pi.GPIO_24
  DIR3: DRV3.DIR, Raspberry_Pi.GPIO_25
  N13: DRV3.2B, M3.A
  N14: DRV3.2A, M3.C
  N15: DRV3.1A, M3.B
  N16: DRV3.1B, M3.D
  3V3: DRV3.VDD, DRV4.VDD, J1.pin4, J1.pin5, J1.pin6, J2.pin4, J2.pin5, J2.pin6, J3.pin4, J3.pin5, J3.pin6, J4.pin4, J4.pin5, J4.pin6, MCP3002.pin8, R3.Pin_1, R1.Pin_1, DRV1.VDD, DRV2.VDD, Raspberry_Pi.3V3
  N17: DRV4.MS1, J4.pin1
  N18: DRV4.MS2, J4.pin2
  N19: DRV4.MS3, J4.pin3
  N20: DRV4.RST, DRV4.SLP
  STEP4: DRV4.STEP, Raspberry_Pi.GPIO_8
  DIR4: DRV4.DIR, Raspberry_Pi.GPIO_4
  N21: DRV4.2B, M4.A
  N22: DRV4.2A, M4.C
  N23: DRV4.1A, M4.B
  N24: DRV4.1B, M4.D
  N25: THERM1.pin1, C2.+, MCP3002.pin2, R1.Pin_0
  N26: HOTEND.pin3, HOTEND.pin4, Q1.drain
  HOTEND: Q1.gate, R2.Pin_1, Raspberry_Pi.GPIO_17
  N27: J1.pin1, DRV1.MS1
  N28: J1.pin2, DRV1.MS2
  N29: J1.pin3, DRV1.MS3
  N30: J2.pin1, DRV2.MS1
  N31: J2.pin2, DRV2.MS2
  N32: J2.pin3, DRV2.MS3
  CS0: MCP3002.pin1, Raspberry_Pi.GPIO_7
  N33: MCP3002.pin3, THERM2.pin1, C7.+, R3.Pin_0
  MOSI: MCP3002.pin5, Raspberry_Pi.GPIO_10
  MISO: MCP3002.pin6, Raspberry_Pi.GPIO_9
  CLK: MCP3002.pin7, Raspberry_Pi.GPIO_11
  N34: HOTBED.pin3, HOTBED.pin4, Q2.drain
  HOTBED: Q2.gate, R4.Pin_1, Raspberry_Pi.GPIO_1
  N35: DRV1.RST, DRV1.SLP
  STEP1: DRV1.STEP, Raspberry_Pi.GPIO_14
  DIR1: DRV1.DIR, Raspberry_Pi.GPIO_15
  N36: DRV2.RST, DRV2.SLP
  STEP2: DRV2.STEP, Raspberry_Pi.GPIO_18
  DIR2: DRV2.DIR, Raspberry_Pi.GPIO_23

notes:
  PiRap, Raspberry Pi RepRap Control Board, 0.1
  Pin1
  Ian D. Miller
  Kenan Bitikofer
  Rev 0.1 2014

custom parts:
  A4983: Poloko A4983 Stepper Motor Control Breakout
